# Fritzing sketch Estacion_Metereologica_blynk_con_alarma (saved by Fritzing 0.8.7b)
breadboards: 1

parts:
  U1 = NodeMCU V1.0
  Part1 = KY-015 Temperature & Humidity Sensor Module [package="Breakout board"]
  YL-83_-_Control_Board1 = YL-83 Rain Sensor - Control Board
  YL-83_-_Detection_Board1 = YL-83 Rain Sensor - Detection Board
  KY-1 = Keyes Relay [package=THT]
  M1 = DC Motor
  VCC1 = Battery block 9V

nets:
  N1: U1.D1, KY-1.signal
  N2: U1.D2, Part1.Vin
  GND: U1.GND, Part1.S, YL-83_-_Control_Board1.GND, KY-1.ground
  VIN: U1.Vin, Part1.-, YL-83_-_Control_Board1.VCC, KY-1.power
  N3: U1.A0, YL-83_-_Control_Board1.AO
  N4: YL-83_-_Control_Board1.POS, YL-83_-_Detection_Board1.POS
  N5: YL-83_-_Control_Board1.NEG, YL-83_-_Detection_Board1.NEG
  N6: KY-1.C, M1.pin_1
  N7: KY-1.NO, VCC1.+

custom parts:
  NodeMCU V1.0: ESP8266 based NodeMCU
  KY-015 Temperature & Humidity Sensor Module: KY-015 temperature and humidity sensor module, provides a low-latency serial interface to measure humidity and temperature.
  YL-83 Rain Sensor - Control Board: The YL-83 is a rain sensor that has more resistance when dry and less resistance when wet. The module runs at 5V.
  YL-83 Rain Sensor - Detection Board: The YL-83 is a rain sensor that has more resistance when dry and less resistance when wet. The module runs at 5V.
  Keyes Relay: The Keyes 5V relay module is suitable for SCM development, home appliance control. It uses a 5V~12V TIL control signal which can control DC / AC signal.
